# Fritzing sketch Устройство управления (saved by Fritzing 0.9.3b)

parts:
  IR1 = TSOP312.., 314.. [package=THT]
  Часть1 = Arduino Uno (Rev3)
  Часть2 = Bluetooth HC-05 Macho
  LED1 = LED - 5mm [color="Infrared (940nm)" package="5 mm [THT]"]

nets:
  GND: IR1.GND, Часть1.GND, Часть2.GND, LED1.cathode
  5V: IR1.Vs, Часть1.5V, Часть2.VCC
  N1: IR1.Data, Часть1.D11_PWM/MOSI
  N2: Часть1.D0/RX, Часть2.TXD
  N3: Часть1.D1/TX, Часть2.RXD
  N4: Часть1.D3_PWM, LED1.anode
